// Logisim project cpu.circ as structural Verilog: 6 circuits, main circuit main
module main (
  input  RESET
);

  wire CLK, control_unit_1_pc_write, control_unit_1_ram_oe;
  wire [1:0] control_unit_1_pc_cmd, control_unit_1_pc_isize;
  wire [15:0] bit_extender_1_out;
  wire [31:0] adder_1_out, control_unit_1_pc_jump_addr, control_unit_1_pc_offset, PROGRAM_COUNTER_address,
       ram_1_data;

  Clock clock_1 (.out(CLK));
  Adder #(.width(32)) adder_1 (
    .a(control_unit_1_pc_offset), .b(PROGRAM_COUNTER_address), .out(adder_1_out), .cin(1'b0));  // open: cout
  COUNTER32b PROGRAM_COUNTER (
    .JUMP_ADDRESS(control_unit_1_pc_jump_addr), .INSTRUCTION_SIZE(control_unit_1_pc_isize),
    .CMD(control_unit_1_pc_cmd), .WRITE(control_unit_1_pc_write), .CLOCK(CLK), .RESET(RESET),
    .ADDRESS(PROGRAM_COUNTER_address));
  RAM #(.addrWidth(16), .asyncread("true"), .dataWidth(32), .databus("bidir")) ram_1 (
    .addr(bit_extender_1_out), .oe(control_unit_1_ram_oe), .clk(CLK), .data(ram_1_data));  // open: we
  Bit_Extender #(.in_width(32), .\type ("zero")) bit_extender_1 (.in(adder_1_out), .out(bit_extender_1_out));
  CONTROL_UNIT control_unit_1 (
    .INSTR_CONST(ram_1_data), .CLOCK(CLK), .RESET(RESET), .RAM_OE(control_unit_1_ram_oe),
    .PC_OFFSET(control_unit_1_pc_offset), .PC_JUMP_ADDR(control_unit_1_pc_jump_addr),
    .PC_ISIZE(control_unit_1_pc_isize), .PC_CMD(control_unit_1_pc_cmd), .PC_WRITE(control_unit_1_pc_write));
endmodule

module RAM_CONTROLLER (
  input  [31:0] WRITEIN,
  input  [20:0] ADDRESS,
  input  WRITESTART,
  input  READSTART,
  input  CLK,
  output [31:0] READOUT
);

  wire and_1_out, and_2_out, and_3_out, d_ff_1_q, d_ff_2_q, d_ff_5_q, demultiplexer_1_out0,
       demultiplexer_1_out1, demultiplexer_2_out0, demultiplexer_2_out1, demultiplexer_2_out2,
       demultiplexer_2_out3, multiplexer_1_out, not_1_out, not_2_out, or_1_out, s_r_ff_1_q, xor_1_out,
       xor_2_out, xor_3_out;
  wire [1:0] d_ff_3_q;
  wire [7:0] multiplexer_2_out, RAM1_data;
  wire [20:0] adder_1_out;

  D_Flip_Flop d_ff_1 (.D(WRITESTART), .clk(CLK), .Q(d_ff_1_q));  // open: Qn, preset, reset
  D_Flip_Flop d_ff_2 (.D(READSTART), .clk(CLK), .Q(d_ff_2_q));  // open: Qn, preset, reset
  and and_1 (and_1_out, WRITESTART, not_1_out);
  not not_1 (not_1_out, d_ff_1_q);
  and and_2 (and_2_out, READSTART, not_2_out);
  not not_2 (not_2_out, d_ff_2_q);
  or or_1 (or_1_out, and_1_out, and_2_out);
  Multiplexer multiplexer_1 (.in0(d_ff_5_q), .in1(and_2_out), .out(multiplexer_1_out), .sel(or_1_out));
  D_Flip_Flop d_ff_3 (.D(xor_1_out), .clk(CLK), .Q(d_ff_3_q[0]), .reset(xor_3_out));  // open: Qn, preset
  xor xor_1 (xor_1_out, d_ff_3_q[0], 1'b1);
  D_Flip_Flop d_ff_4 (.D(xor_2_out), .clk(CLK), .Q(d_ff_3_q[1]), .reset(xor_3_out));  // open: Qn, preset
  xor xor_2 (xor_2_out, d_ff_3_q[1], d_ff_3_q[0]);
  Adder #(.width(21)) adder_1 (.a({{19{1'b0}}, d_ff_3_q}), .b(ADDRESS), .out(adder_1_out), .cin(1'b0));  // open: cout
  S_R_Flip_Flop s_r_ff_1 (.S(or_1_out), .R(and_3_out), .clk(CLK), .Q(s_r_ff_1_q));  // open: reset, Qn, preset
  D_Flip_Flop d_ff_5 (.D(multiplexer_1_out), .clk(CLK), .Q(d_ff_5_q));  // open: Qn, preset, reset
  xor xor_3 (xor_3_out, 1'b1, s_r_ff_1_q);
  and and_3 (and_3_out, d_ff_3_q[0], d_ff_3_q[1]);
  Demultiplexer demultiplexer_1 (
    .out0(demultiplexer_1_out0), .out1(demultiplexer_1_out1), .in(s_r_ff_1_q), .sel(d_ff_5_q));
  RAM #(.addrWidth(21), .asyncread("true"), .databus("bidir")) RAM1 (
    .addr(adder_1_out), .we(demultiplexer_1_out0), .oe(demultiplexer_1_out1), .clk(CLK), .data(RAM1_data));
  Multiplexer #(.select(2), .width(8)) multiplexer_2 (
    .in0(WRITEIN[31:24]), .in1(WRITEIN[23:16]), .in2(WRITEIN[15:8]), .in3(WRITEIN[7:0]),
    .out(multiplexer_2_out), .sel(d_ff_3_q));
  assign RAM1_data = demultiplexer_1_out0 ? multiplexer_2_out : 8'bz;  // Controlled_Buffer controlled_buffer_1
  Demultiplexer #(.select(2)) demultiplexer_2 (
    .out0(demultiplexer_2_out0), .out1(demultiplexer_2_out1), .out2(demultiplexer_2_out2),
    .out3(demultiplexer_2_out3), .in(demultiplexer_1_out1), .sel(d_ff_3_q));
  Register register_1 (.D(RAM1_data), .en(demultiplexer_2_out0), .clk(CLK), .Q(READOUT[31:24]));  // open: clr
  Register register_2 (.D(RAM1_data), .en(demultiplexer_2_out1), .clk(CLK), .Q(READOUT[23:16]));  // open: clr
  Register register_3 (.D(RAM1_data), .en(demultiplexer_2_out2), .clk(CLK), .Q(READOUT[15:8]));  // open: clr
  Register register_4 (.D(RAM1_data), .en(demultiplexer_2_out3), .clk(CLK), .Q(READOUT[7:0]));  // open: clr
endmodule

module REGISTER32b (
  input  [31:0] DATA,
  input  WRITE,
  input  CLOCK,
  input  RESET,
  output [31:0] STORED
);

  Register #(.width(32)) register_1 (.D(DATA), .en(WRITE), .clk(CLOCK), .Q(STORED), .clr(RESET));
  Hex_Digit_Display hex_digit_display_1 (.value(STORED[31:28]));  // open: dp
  Hex_Digit_Display hex_digit_display_2 (.value(STORED[27:24]));  // open: dp
  Hex_Digit_Display hex_digit_display_3 (.value(STORED[23:20]));  // open: dp
  Hex_Digit_Display hex_digit_display_4 (.value(STORED[19:16]));  // open: dp
  Hex_Digit_Display hex_digit_display_5 (.value(STORED[15:12]));  // open: dp
  Hex_Digit_Display hex_digit_display_6 (.value(STORED[11:8]));  // open: dp
  Hex_Digit_Display hex_digit_display_7 (.value(STORED[7:4]));  // open: dp
  Hex_Digit_Display hex_digit_display_8 (.value(STORED[3:0]));  // open: dp
endmodule

module COUNTER32b (
  input  [31:0] JUMP_ADDRESS,
  input  [1:0] INSTRUCTION_SIZE,
  input  CLOCK,
  input  RESET,
  input  [1:0] CMD,
  input  WRITE,
  output [31:0] ADDRESS
);

  wire [31:0] adder_1_out, bit_extender_1_out, multiplexer_1_out;

  Adder #(.width(32)) adder_1 (.a(ADDRESS), .b(bit_extender_1_out), .out(adder_1_out), .cin(1'b0));  // open: cout
  assign bit_extender_1_out = {{30{1'b0}}, INSTRUCTION_SIZE};  // Bit_Extender bit_extender_1
  Multiplexer #(.select(2), .width(32)) multiplexer_1 (
    .in0(ADDRESS), .in1(adder_1_out), .in2(JUMP_ADDRESS), .in3({32{1'b0}}), .out(multiplexer_1_out), .sel(CMD));
  REGISTER32b register32b_1 (.DATA(multiplexer_1_out), .WRITE(WRITE), .CLOCK(CLOCK), .RESET(RESET), .STORED(ADDRESS));
endmodule

module CONTROL_UNIT (
  input  [31:0] INSTR_CONST,
  input  CLOCK,
  input  RESET,
  output RAM_OE,
  output [31:0] PC_OFFSET,
  output [31:0] PC_JUMP_ADDR,
  output [1:0] PC_ISIZE,
  output [1:0] PC_CMD,
  output PC_WRITE
);

  wire and_1_out, ICODE_0000, JUMP, JUMP_END, not_1_out, not_2_out, not_3_out, not_4_out, OPTYPE_ALU,
       OPTYPE_CTRLFLOW, OPTYPE_DATA, or_1_out, or_2_out, or_3_out, START, START_D1;
  wire [1:0] controlled_buffer_2_out, controlled_buffer_3_out;

  D_Flip_Flop u_START (.D(PC_WRITE), .clk(CLOCK), .Q(START), .preset(RESET), .reset(1'b0));  // open: Qn
  D_Flip_Flop u_START_D1 (.D(START), .clk(CLOCK), .Q(START_D1), .preset(1'b0), .reset(RESET));  // open: Qn
  assign PC_OFFSET = JUMP_END ? 32'h1 : 32'bz;  // Controlled_Buffer controlled_buffer_1
  assign controlled_buffer_2_out = JUMP_END ? 2'b10 : 2'bz;  // Controlled_Buffer controlled_buffer_2
  assign controlled_buffer_3_out = START ? 2'b01 : 2'bz;  // Controlled_Buffer controlled_buffer_3
  assign controlled_buffer_2_out = START ? 2'b01 : 2'bz;  // Controlled_Buffer controlled_buffer_4
  or or_1 (or_1_out, START, JUMP_END);
  Register #(.width(32)) register_1 (.D(INSTR_CONST), .en(JUMP_END), .clk(CLOCK), .Q(PC_JUMP_ADDR), .clr(RESET));
  Register #(.width(2)) register_2 (.D(controlled_buffer_3_out), .en(START), .clk(CLOCK), .Q(PC_ISIZE), .clr(RESET));
  Register #(.width(2)) register_3 (.D(controlled_buffer_2_out), .en(or_1_out), .clk(CLOCK), .Q(PC_CMD), .clr(RESET));
  D_Flip_Flop FETCH (.D(or_2_out), .clk(CLOCK), .Q(RAM_OE), .preset(1'b0), .reset(RESET));  // open: Qn
  or or_2 (or_2_out, JUMP, START);
  Pull_Resistor pull_resistor_1 (.node(PC_OFFSET));
  not not_1 (not_1_out, INSTR_CONST[28]);
  nor nor_1 (OPTYPE_DATA, not_1_out, INSTR_CONST[29], INSTR_CONST[30], INSTR_CONST[31]);
  not not_2 (not_2_out, INSTR_CONST[29]);
  nor nor_2 (OPTYPE_ALU, INSTR_CONST[28], not_2_out, INSTR_CONST[30], INSTR_CONST[31]);
  not not_3 (not_3_out, INSTR_CONST[28]);
  not not_4 (not_4_out, INSTR_CONST[29]);
  nor nor_3 (OPTYPE_CTRLFLOW, not_3_out, not_4_out, INSTR_CONST[30], INSTR_CONST[31]);
  D_Flip_Flop STEP (.D(or_3_out), .clk(CLOCK), .Q(PC_WRITE), .preset(1'b0), .reset(RESET));  // open: Qn
  buf or_3 (or_3_out, JUMP_END);  // OR_Gate
  nor nor_4 (ICODE_0000, INSTR_CONST[24], INSTR_CONST[25], INSTR_CONST[26], INSTR_CONST[27]);
  D_Flip_Flop u_JUMP (.D(and_1_out), .clk(CLOCK), .Q(JUMP), .preset(1'b0), .reset(RESET));  // open: Qn
  and and_1 (and_1_out, OPTYPE_CTRLFLOW, ICODE_0000, START_D1);
  D_Flip_Flop u_JUMP_END (.D(JUMP), .clk(CLOCK), .Q(JUMP_END), .preset(1'b0), .reset(RESET));  // open: Qn

  // Other names for the same wires on the sheet: CLK = CLOCK; CONST[31:0] = INSTR_CONST; FETCH = RAM_OE;
  //   STEP = PC_WRITE
endmodule

module REGISTERS_ARRAY (
  input  [31:0] DATA,
  input  [1:0] MODE,
  input  [3:0] SELECT_A,
  input  [3:0] SELECT_B,
  output [31:0] OUT_A,
  output [31:0] OUT_B
);

  wire undriven, undriven_2, undriven_3, undriven_4, undriven_5, undriven_6, undriven_7, undriven_8,
       undriven_9, undriven_10, undriven_11, undriven_12, undriven_13, undriven_14, undriven_15, undriven_16;
  wire [31:0] controlled_buffer_1_out, controlled_buffer_17_out, register32b_1_stored, register32b_2_stored,
       register32b_3_stored, register32b_4_stored, register32b_5_stored, register32b_6_stored,
       register32b_7_stored, register32b_8_stored, register32b_9_stored, register32b_10_stored,
       register32b_11_stored, register32b_12_stored, register32b_13_stored, register32b_14_stored,
       register32b_15_stored, register32b_16_stored;

  assign controlled_buffer_1_out = undriven ? register32b_1_stored : 32'bz;  // Controlled_Buffer controlled_buffer_1
  REGISTER32b register32b_1 (.STORED(register32b_1_stored));  // open: DATA, WRITE, CLOCK, RESET
  REGISTER32b register32b_2 (.STORED(register32b_2_stored));  // open: DATA, WRITE, CLOCK, RESET
  REGISTER32b register32b_3 (.STORED(register32b_3_stored));  // open: DATA, WRITE, CLOCK, RESET
  REGISTER32b register32b_4 (.STORED(register32b_4_stored));  // open: DATA, WRITE, CLOCK, RESET
  REGISTER32b register32b_5 (.STORED(register32b_5_stored));  // open: DATA, WRITE, CLOCK, RESET
  REGISTER32b register32b_6 (.STORED(register32b_6_stored));  // open: DATA, WRITE, CLOCK, RESET
  REGISTER32b register32b_7 (.STORED(register32b_7_stored));  // open: DATA, WRITE, CLOCK, RESET
  REGISTER32b register32b_8 (.STORED(register32b_8_stored));  // open: DATA, WRITE, CLOCK, RESET
  REGISTER32b register32b_9 (.STORED(register32b_9_stored));  // open: DATA, WRITE, CLOCK, RESET
  REGISTER32b register32b_10 (.STORED(register32b_10_stored));  // open: DATA, WRITE, CLOCK, RESET
  REGISTER32b register32b_11 (.STORED(register32b_11_stored));  // open: DATA, WRITE, CLOCK, RESET
  REGISTER32b register32b_12 (.STORED(register32b_12_stored));  // open: DATA, WRITE, CLOCK, RESET
  REGISTER32b register32b_13 (.STORED(register32b_13_stored));  // open: DATA, WRITE, CLOCK, RESET
  REGISTER32b register32b_14 (.STORED(register32b_14_stored));  // open: DATA, WRITE, CLOCK, RESET
  REGISTER32b register32b_15 (.STORED(register32b_15_stored));  // open: DATA, WRITE, CLOCK, RESET
  REGISTER32b register32b_16 (.STORED(register32b_16_stored));  // open: DATA, WRITE, CLOCK, RESET
  Controlled_Buffer #(.width(32)) controlled_buffer_2 (.in(register32b_2_stored), .en(undriven_2));  // open: out
  Controlled_Buffer #(.width(32)) controlled_buffer_3 (.in(register32b_3_stored), .en(undriven_3));  // open: out
  Controlled_Buffer #(.width(32)) controlled_buffer_4 (.in(register32b_4_stored), .en(undriven_4));  // open: out
  Controlled_Buffer #(.width(32)) controlled_buffer_5 (.in(register32b_5_stored), .en(undriven_5));  // open: out
  Controlled_Buffer #(.width(32)) controlled_buffer_6 (.in(register32b_6_stored), .en(undriven_6));  // open: out
  Controlled_Buffer #(.width(32)) controlled_buffer_7 (.in(register32b_7_stored), .en(undriven_7));  // open: out
  Controlled_Buffer #(.width(32)) controlled_buffer_8 (.in(register32b_8_stored), .en(undriven_8));  // open: out
  Controlled_Buffer #(.width(32)) controlled_buffer_9 (.in(register32b_9_stored));  // open: out, en
  Controlled_Buffer #(.width(32)) controlled_buffer_10 (.in(register32b_10_stored));  // open: out, en
  Controlled_Buffer #(.width(32)) controlled_buffer_11 (.in(register32b_11_stored));  // open: out, en
  Controlled_Buffer #(.width(32)) controlled_buffer_12 (.in(register32b_12_stored));  // open: out, en
  Controlled_Buffer #(.width(32)) controlled_buffer_13 (.in(register32b_13_stored));  // open: out, en
  Controlled_Buffer #(.width(32)) controlled_buffer_14 (.in(register32b_14_stored));  // open: out, en
  Controlled_Buffer #(.width(32)) controlled_buffer_15 (.in(register32b_15_stored));  // open: out, en
  Controlled_Buffer #(.width(32)) controlled_buffer_16 (.in(register32b_16_stored));  // open: out, en
  assign controlled_buffer_17_out = undriven_9 ? register32b_1_stored : 32'bz;  // Controlled_Buffer controlled_buffer_17
  Controlled_Buffer #(.width(32)) controlled_buffer_18 (.in(register32b_2_stored), .en(undriven_10));  // open: out
  Controlled_Buffer #(.width(32)) controlled_buffer_19 (.in(register32b_3_stored), .en(undriven_11));  // open: out
  Controlled_Buffer #(.width(32)) controlled_buffer_20 (.in(register32b_4_stored), .en(undriven_12));  // open: out
  Controlled_Buffer #(.width(32)) controlled_buffer_21 (.in(register32b_5_stored), .en(undriven_13));  // open: out
  Controlled_Buffer #(.width(32)) controlled_buffer_22 (.in(register32b_6_stored), .en(undriven_14));  // open: out
  Controlled_Buffer #(.width(32)) controlled_buffer_23 (.in(register32b_7_stored), .en(undriven_15));  // open: out
  Controlled_Buffer #(.width(32)) controlled_buffer_24 (.in(register32b_8_stored), .en(undriven_16));  // open: out
  Controlled_Buffer #(.width(32)) controlled_buffer_25 (.in(register32b_9_stored));  // open: out, en
  Controlled_Buffer #(.width(32)) controlled_buffer_26 (.in(register32b_10_stored));  // open: out, en
  Controlled_Buffer #(.width(32)) controlled_buffer_27 (.in(register32b_11_stored));  // open: out, en
  Controlled_Buffer #(.width(32)) controlled_buffer_28 (.in(register32b_12_stored));  // open: out, en
  Controlled_Buffer #(.width(32)) controlled_buffer_29 (.in(register32b_13_stored));  // open: out, en
  Controlled_Buffer #(.width(32)) controlled_buffer_30 (.in(register32b_14_stored));  // open: out, en
  Controlled_Buffer #(.width(32)) controlled_buffer_31 (.in(register32b_15_stored));  // open: out, en
  Controlled_Buffer #(.width(32)) controlled_buffer_32 (.in(register32b_16_stored));  // open: out, en
endmodule
